# Fritzing sketch schematic_v02-breadboard-promini (saved by Fritzing 0.8.5b)
breadboards: 1

parts:
  Part2 = Arduino Pro Mini v13
  SP2 = SPEAKER [package=pcb_mount_speaker]
  U2 = POT [package=pot_alpha_rv16af-20]
  S2 = Pushbutton [package="[THT]"]
  S3 = Pushbutton [package="[THT]"]
  RGB_light_strings1 = mystery part, 4 pins [chip_label=RGB]
  Power_supply_5V_12A = Power plug
  R4 = Resistor [tolerance=±5% resistance=10k package=THT]
  R5 = Resistor [tolerance=±5% resistance=100 package=THT]
  R6 = Resistor [tolerance=±5% resistance=10k package=THT]

nets:
  N1: Part2.RAW, RGB_light_strings1.pin3, Power_supply_5V_12A.VCC
  GND: Part2.GND, SP2.+, U2.A, RGB_light_strings1.pin1, RGB_light_strings1.pin4, Power_supply_5V_12A.GND, R4.Pin_1, R6.Pin_1
  N2: Part2.VCC, U2.E, S2.Pin_3, S3.Pin_3
  N3: Part2.A0, U2.S
  N4: Part2.D8, R5.Pin_1
  N5: Part2.D6_PWM, RGB_light_strings1.pin2
  N6: Part2.D4, S3.Pin_1, R6.Pin_0
  N7: Part2.D3_PWM, S2.Pin_1, R4.Pin_0
  N8: SP2.-, R5.Pin_0
